# Fritzing sketch Arduino Uno Encoder (saved by Fritzing 0.9.3b)
breadboards: 1

parts:
  Part1 = Arduino Uno (Rev3)
  ENCODER2 = Rotary Encoder with Knob
  X2 = X113647 Stepper Driver Board [package=board]
  MOTOR2 = 28BYJ-48 Stepper Motor  # not connected
  YwRobot_Power_Supply1 = YwRobot Breadboard Power Supply [part_number=545043]

nets:
  N1: Part1.D8, X2.IN4
  N2: Part1.D9_PWM, X2.IN3
  N3: Part1.D10_PWM/SS, X2.IN2
  N4: Part1.D11_PWM/MOSI, X2.IN1
  N5: Part1.D2, ENCODER2.CLK
  N6: Part1.D3_PWM, ENCODER2.DT
  N7: Part1.D4, ENCODER2.SW
  N8: Part1.5V, ENCODER2.+, X2.+V, YwRobot_Power_Supply1.VCC#9
  GND: Part1.GND, ENCODER2.GND, X2.GND, YwRobot_Power_Supply1.GND#13

notes:
  Rotary Encoder
  KY-040
  int 1
  int 2
  int 3
  int 4
  CLK
  DT
  SW
  +
  GND

custom parts:
  Rotary Encoder with Knob: Rotary Encoder with 1/4" Shaft and Knob
  X113647 Stepper Driver Board: A common stepper motor driver board based on ULN2003APG darlington array
  28BYJ-48 Stepper Motor: 28BYJ-48 gear-reduction stepper motor (small)
  YwRobot Breadboard Power Supply: The YwRobot Breadboard Power Supply (MB-V2) has two power rails; they can be 5V or 3V3. Power to the module can be provided through the female USB socket or through the A10 (female) 2.1mm power jack.
